# Fritzing sketch Esquema eléctrico (saved by Fritzing 0.9.3b)
breadboards: 1

parts:
  Arduino1 = Arduino Uno (Rev3)
  J1 = Piezo Speaker

nets:
  N1: Arduino1.D13/SCK, J1.pin2
  N2: Arduino1.GND, J1.pin1
