# Fritzing sketch Esquema eléctrico (saved by Fritzing 0.9.3b)
breadboards: 1

parts:
  Arduino1 = Arduino Uno (Rev3)
  LED1 = LED - 5mm [color="White (4500K)" package="5 mm [THT]"]
  R1 = Resistor [tolerance=±5% resistance=100 package=THT]
  R2 = Resistor [tolerance=±5% resistance=10k package=THT]
  R3 = Photocell (LDR) [package=THT]

nets:
  N1: Arduino1.A0, R2.Pin_1, R3.pin_0
  N2: Arduino1.D13/SCK, LED1.anode
  N3: Arduino1.GND, R1.Pin_0, R2.Pin_0
  N4: Arduino1.5V, R3.pin_1
  N5: LED1.cathode, R1.Pin_1
