# Fritzing sketch Esquema eléctrico (saved by Fritzing 0.9.3b)
breadboards: 1

parts:
  Arduino1 = Arduino Uno (Rev3)
  R1 = Photocell (LDR) [package=THT]
  R2 = Resistor [tolerance=±5% resistance=220 package=THT]
  LED1 = RGB LED (com. cathode, rgb) [package="5 mm [THT]"]
  R3 = Resistor [tolerance=±5% resistance=220 package=THT]
  R4 = Resistor [tolerance=±5% resistance=100 package=THT]
  R5 = Resistor [tolerance=±5% resistance=100 package=THT]

nets:
  N1: Arduino1.A0, R1.pin_1, R2.Pin_0
  N2: Arduino1.D9_PWM, R3.Pin_1
  N3: Arduino1.GND, R2.Pin_1
  N4: Arduino1.D5_PWM, R5.Pin_1
  N5: Arduino1.D6_PWM, R4.Pin_1
  N6: Arduino1.5V, R1.pin_0, LED1.common_cathode
  N7: LED1.red_anode, R3.Pin_0
  N8: LED1.green_anode, R4.Pin_0
  N9: LED1.blue_anode, R5.Pin_0
