# Fritzing sketch Esquema-eléctrico (saved by Fritzing 0.9.3b)
breadboards: 1

parts:
  Arduino1 = Arduino Uno (Rev3)
  J1 = Basic Servo
  R1 = Rotary Potentiometer (Small) [maximum_resistance=0.1MΩ package=THT]

nets:
  N1: Arduino1.A0, R1.leg2
  N2: Arduino1.D9_PWM, J1.pulse
  GND: Arduino1.GND, J1.gnd, R1.wiper
  5V: Arduino1.5V, J1.vcc, R1.leg1
