# Fritzing sketch Esquema eléctrico (saved by Fritzing 0.9.3b)
breadboards: 1

parts:
  Arduino1 = Arduino Uno (Rev3)
  hc-sr1 = hc-sr04
  J1 = Piezo Speaker

nets (from the schematic view):
  N1: Arduino1.D11_PWM/MOSI, hc-sr1.Echo
  5V: Arduino1.D12/MISO, Arduino1.5V, hc-sr1.VCC, hc-sr1.Trig
  N2: Arduino1.D13/SCK, J1.pin2
  GND: Arduino1.GND, hc-sr1.GND, J1.pin1
