# Fritzing sketch Esquema eléctrico (saved by Fritzing 0.9.3b)
breadboards: 1

parts:
  Arduino1 = Arduino Uno (Rev3)
  hc-sr1 = hc-sr04

nets:
  N1: Arduino1.D12/MISO, hc-sr1.Echo
  N2: Arduino1.D13/SCK, hc-sr1.Trig
  GND: Arduino1.GND, hc-sr1.GND
  5V: Arduino1.5V, hc-sr1.VCC
