# Fritzing sketch Esquema-eléctrico (saved by Fritzing 0.9.3b)
breadboards: 1

parts:
  Arduino1 = Arduino Uno (Rev3)
  LED1 = LED - 5mm [color="White (4500K)" package="5 mm [THT]"]
  LED2 = LED - 5mm [color="White (4500K)" package="5 mm [THT]"]
  LED3 = LED - 5mm [color="White (4500K)" package="5 mm [THT]"]
  R1 = Resistor [tolerance=±5% resistance=100 package=THT]
  R2 = Resistor [tolerance=±5% resistance=100 package=THT]
  R3 = Resistor [tolerance=±5% resistance=100 package=THT]
  R4 = Trimmer Potentiometer [maximum_resistance=10kΩ package=THT]

nets:
  N1: Arduino1.A0, R4.wiper
  N2: Arduino1.D9_PWM, LED1.anode
  N3: Arduino1.GND, R1.Pin_1, R2.Pin_1, R3.Pin_1, R4.leg1
  N4: Arduino1.D5_PWM, LED3.anode
  N5: Arduino1.D6_PWM, LED2.anode
  N6: Arduino1.5V, R4.leg2
  N7: LED1.cathode, R1.Pin_0
  N8: LED2.cathode, R2.Pin_0
  N9: LED3.cathode, R3.Pin_0
