# Fritzing sketch Esquema-eléctrico (saved by Fritzing 0.9.3b)
breadboards: 1

parts:
  Arduino1 = Arduino Uno (Rev3)
  LED1 = LED - 5mm [color="Red (633nm)" package="5 mm [THT]"]
  R1 = Resistor [tolerance=±5% resistance=220 package=THT]
  R2 = Resistor [tolerance=±5% resistance=10k package=THT]
  S5 = Pushbutton [package="[SMD]"]

nets:
  N1: Arduino1.D13/SCK, LED1.anode
  N2: Arduino1.GND, R1.Pin_0, R2.Pin_0
  N3: Arduino1.D2, R2.Pin_1, S5.Pin_3, S5.Pin_4
  N4: Arduino1.5V, S5.Pin_1, S5.Pin_2
  N5: LED1.cathode, R1.Pin_1
