# Fritzing sketch Fritzing (saved by Fritzing 0.8.6b)
breadboards: 1

parts:
  Parte1 = Arduino Uno (Rev3)
  IC1 = L293D [package=THT]
  BAT1 = BC9VPC [package=bc9vpc]
  M1 = DC Motor
  S4 = SWITCH-MOMENTARY-2 [package=tactile-switch-1101ne]
  R4 = Resistor [tolerance=±5% resistance=1k package="1206 [SMD]"]
  R3 = Resistor [tolerance=±5% resistance=1k package="1206 [SMD]"]
  S3 = SWITCH-MOMENTARY-2 [package=tactile-switch-1101ne]

nets:
  N1: Parte1.D10_PWM/SS, IC1.In_3
  N2: Parte1.D11_PWM/MOSI, IC1.In_4
  N3: Parte1.GND, IC1.0V, BAT1.V+, R4.Pin_1, R3.Pin_1
  N4: Parte1.D2, S4.2, R4.Pin_0
  N5: Parte1.D3_PWM, R3.Pin_0, S3.2
  N6: Parte1.5V, IC1.+Vmotor, IC1.Enable_2, S4.1, S3.1
  N7: IC1.Out_3_(_Controlled_by_Enable_2_), M1.pin_1
  N8: IC1.Out_4_(_Controlled_by_Enable_2_), M1.pin_2
  N9: IC1.+V, BAT1.V-
