# Fritzing sketch Fritzing (saved by Fritzing 0.6.5b)
breadboards: 1

parts:
  Arduino1 = Arduino
  J1 = Basic Servo
  LED1 = LED - 5mm [color="Red (633nm)" package="5 mm [THT]"]
  R1 = Rotary Potentiometer (Small) [maximum_resistance=100kΩ]
  R2 = Resistor [tolerance=±5% resistance=220 package=THT]
  LED2 = LED - 5mm [color="Green (570nm)" package="5 mm [THT]"]
  R3 = Resistor [tolerance=±5% resistance=220 package=THT]

nets:
  GND: Arduino1.GND, J1.gnd, R1.leg1, R2.Pin_0, R3.Pin_0
  N1: Arduino1.D13, LED1.anode
  N2: Arduino1.D12, LED2.anode
  N3: Arduino1.D9, J1.pulse
  +5V: Arduino1.+5V, J1.vcc, R1.leg2
  N4: Arduino1.A0, R1.wiper
  N5: LED1.cathode, R2.Pin_1
  N6: LED2.cathode, R3.Pin_1
