# Fritzing sketch Fritzing (saved by Fritzing 0.8.6b)
breadboards: 1

parts:
  R1 = Resistor [tolerance=±5% resistance=220 package=THT]
  LED1 = LED - 5mm [color="Green (555nm)" package="5 mm [THT]"]
  LED2 = LED - 5mm [color="Red (633nm)" package="5 mm [THT]"]
  R3 = Photocell (LDR) [package=THT]
  R4 = Resistor [tolerance=±5% resistance=220 package=THT]
  Parte1 = Arduino Uno (Rev3)
  J1 = Basic Servo
  R2 = Resistor [tolerance=±2% resistance=10k package="0805 [SMD]"]  # not connected

nets:
  N1: R1.Pin_0, LED2.cathode
  GND: R1.Pin_1, R4.Pin_1, Parte1.GND, J1.gnd
  N2: LED1.cathode, R4.Pin_0
  N3: LED1.anode, Parte1.D12/MISO
  N4: LED2.anode, Parte1.D13/SCK
  N5: R3.pin_0, Parte1.A0
  N6: R3.pin_1, Parte1.5V, J1.pulse
  N7: Parte1.D9_PWM, J1.vcc
