# Fritzing sketch Fritzing (saved by Fritzing 0.9.3b)
breadboards: 1

parts:
  Componente1 = Arduino Uno (Rev3)
  J1 = Basic Servo
  R1 = Photocell (LDR) [package=THT]
  R2 = Resistor [tolerance=±5% resistance=100 package=THT]

nets:
  N1: Componente1.D9_PWM, J1.pulse
  GND: Componente1.GND, J1.gnd, R2.Pin_0
  5V: Componente1.5V, J1.vcc, R1.pin_1
  N2: R1.pin_0, R2.Pin_1
