# Fritzing sketch Fritzing (saved by Fritzing 0.9.3b)
breadboards: 1

parts:
  Componente1 = Arduino Uno (Rev3)
  J1 = Piezo Speaker
  LED1 = LED - 5mm [color="Red (633nm)" package="5 mm [THT]"]
  R1 = Resistor [tolerance=±5% resistance=220 package=THT]

nets:
  N1: Componente1.D9_PWM, J1.pin2
  N2: Componente1.D11_PWM/MOSI, LED1.anode
  N3: Componente1.5V, J1.pin1, R1.Pin_1
  N4: LED1.cathode, R1.Pin_0
