# Fritzing sketch Fritzing (saved by Fritzing 0.8.6b)
breadboards: 1

parts:
  Parte1 = Arduino Uno (Rev3)
  J1 = Basic Servo
  S1 = Pushbutton [package="[THT]"]
  R1 = Resistor [tolerance=±5% resistance=100 package=THT]

nets:
  N1: Parte1.D9_PWM, J1.pulse
  GND: Parte1.GND, J1.gnd, R1.Pin_0
  N2: Parte1.D4, R1.Pin_1
  N3: Parte1.3V3, S1.Pin_3, S1.Pin_4
  5V: Parte1.5V, J1.vcc
