# Fritzing sketch Fritzing (saved by Fritzing 0.9.3b)

parts:
  Componente1 = Arduino Uno (Rev3)  # not connected
  Componente2 = Arduino Sensor Shield v5.0
  S1 = H-Bridge with L298N
  hc-sr1 = hc-sr04
  J1 = Basic Servo  # not connected
  M1 = DC Motor
  M2 = DC Motor  # not connected
  M3 = DC Motor  # not connected
  M4 = DC Motor
  VCC2 = Battery  # not connected
  VCC4 = Battery block 9V  # not connected
  VCC5 = Battery
  VCC6 = Battery  # not connected
  VCC7 = Battery

nets:
  N1: Componente2.A4, hc-sr1.Trig
  N2: Componente2.A5, hc-sr1.Echo
  N3: Componente2.D10, S1.IN3
  N4: Componente2.D11, S1.IN4
  N5: Componente2.D5, S1.IN1
  N6: Componente2.D6, S1.IN2
  +5V: Componente2.+5V, hc-sr1.VCC
  GND: Componente2.GND, hc-sr1.GND
  N7: S1.12V, VCC5.+
  N8: S1.GND, VCC7.-
  N9: S1.OUT3-Motor2, M1.pin_2, M4.pin_2
  N10: S1.OUT4-Motor2, M1.pin_1, M4.pin_1

custom parts:
  H-Bridge with L298N: h-bridge
