# Fritzing sketch Fritzing-Cuadratura (saved by Fritzing 0.9.1b)
breadboards: 1

parts:
  R1 = Resistor [tolerance=±5% resistance=220 package=THT]
  R2 = Resistor [tolerance=±5% resistance=1k package=THT]
  LED1 = LED - 5mm [color="Green (560nm)" package="5 mm [THT]"]
  LED2 = LED - 5mm [color="Red (633nm)" package="5 mm [THT]"]
  Parte1 = Arduino Uno (Rev3)

nets:
  N1: R1.Pin_0, LED1.anode
  N2: R1.Pin_1, Parte1.D13/SCK
  N3: R2.Pin_0, LED2.anode
  N4: R2.Pin_1, Parte1.D12/MISO
  N5: LED1.cathode, LED2.cathode, Parte1.GND
