# Fritzing sketch Fritzing-Sensor (saved by Fritzing 0.9.2b)
breadboards: 1

parts:
  Parte1 = Arduino Uno (Rev3)
  T1 = LM35 Temperature Sensor [package="TO92 [THT]"]
  LED1 = smd LED [color="Red (633nm)" package="0603 [SMD]"]
  LED2 = smd LED [color="Red (633nm)" package="0603 [SMD]"]
  LED3 = smd LED [color="Red (633nm)" package="0603 [SMD]"]
  R1 = Resistor [tolerance=±5% resistance=220 package=THT]
  R2 = Resistor [tolerance=±5% resistance=220 package=THT]
  R3 = Resistor [tolerance=±5% resistance=220 package=THT]

nets:
  N1: Parte1.A0, T1.Vout
  GND: Parte1.GND, T1.GND, R1.Pin_0, R2.Pin_0, R3.Pin_0
  N2: Parte1.D2, LED3.anode
  N3: Parte1.D3_PWM, LED2.anode
  N4: Parte1.D4, LED1.anode
  N5: Parte1.5V, T1.+Vs
  N6: LED1.cathode, R3.Pin_1
  N7: LED2.cathode, R2.Pin_1
  N8: LED3.cathode, R1.Pin_1
