# Fritzing sketch Fritzing (saved by Fritzing 0.9.3b)
breadboards: 1

parts:
  Componente1 = Arduino Uno (Rev3)
  M1 = Stepper Motor - Bipolar
  R1 = Trimmer Potentiometer [maximum_resistance=10kΩ package=THT]
  R2 = Photocell (LDR) [package=THT]
  R3 = Resistor [tolerance=±5% resistance=220 package=THT]

nets:
  N1: Componente1.A0, R1.wiper
  N2: Componente1.A1, R1.leg1
  N3: Componente1.A2, R2.pin_0, R3.Pin_1
  N4: Componente1.D8, M1.A
  N5: Componente1.D9_PWM, M1.B
  N6: Componente1.D10_PWM/SS, M1.C
  N7: Componente1.D11_PWM/MOSI, M1.D
  N8: Componente1.5V, R2.pin_1
  N9: Componente1.GND, R1.leg2, R3.Pin_0
