# Fritzing sketch Fritzing (saved by Fritzing 0.9.3b)
breadboards: 1

parts:
  Componente1 = Arduino Uno (Rev3)
  R1 = Resistor [tolerance=±5% resistance=10k package=THT]
  R2 = Photocell (LDR) [package=THT]
  J1 = Basic Servo

nets:
  N1: Componente1.A0, R1.Pin_1, R2.pin_0
  5V: Componente1.5V, R2.pin_1, J1.vcc
  GND: Componente1.GND, R1.Pin_0, J1.gnd
