# Fritzing sketch Fritzing (saved by Fritzing 0.9.3b)
breadboards: 1

parts:
  S1 = H-Bridge with L298N
  R1 = Resistor [tolerance=±5% resistance=10k package=THT]
  Componente1 = Arduino Uno (Rev3)
  R2 = Photocell (LDR) [package=THT]
  M1 = DC Motor
  VCC1 = Battery

nets (from the breadboard view):
  N1: S1.12V, VCC1.+
  GND: S1.GND, Componente1.GND, VCC1.-
  5V: S1.5V, Componente1.VIN
  N2: S1.IN3, Componente1.D10_PWM/SS
  N3: S1.IN4, Componente1.D9_PWM
  N4: S1.M2-01, M1.pin_2
  N5: S1.M2-02, M1.pin_1
  N6: R1.Pin_1, R2.pin_0
  N7: Componente1.5V, R2.pin_1

custom parts:
  H-Bridge with L298N: h-bridge
