# Fritzing sketch Fritzing (saved by Fritzing 0.8.6b)
breadboards: 1

parts:
  Parte1 = Arduino Ethernet Shield (Rev3)
  R2 = Resistor [tolerance=±5% resistance=220 package=THT]
  R3 = Resistor [tolerance=±5% resistance=220 package=THT]
  LED2 = LED - 5mm [color="Green (570nm)" package="5 mm [THT]"]
  S1 = Pushbutton [package="[THT]"]
  R4 = Resistor [tolerance=±5% resistance=10k package=THT]
  LED3 = LED - 5mm [color="Yellow (592nm)" package="5 mm [THT]"]
  R6 = Resistor [tolerance=±5% resistance=220 package=THT]
  J1 = Basic Servo
  LED1 = LED - 5mm [color="Red (633nm)" package="5 mm [THT]"]

nets (from the breadboard view):
  5V: Parte1.5V, S1.Pin_1, S1.Pin_2, J1.vcc
  GND: Parte1.GND, LED2.cathode, R4.Pin_0, LED3.cathode, J1.gnd, LED1.cathode
  N1: Parte1.PWM_D11, R2.Pin_0
  N2: Parte1.SPI/D12, R6.Pin_0
  N3: Parte1.A2, S1.Pin_3, S1.Pin_4, R4.Pin_1
  N4: Parte1.PWM_D6, R3.Pin_0
  N5: R2.Pin_1, LED2.anode
  N6: R3.Pin_1, LED3.anode
  N7: R6.Pin_1, LED1.anode
