# Fritzing sketch Fritzing (saved by Fritzing 0.9.3b)
breadboards: 1

parts:
  Componente1 = Arduino Uno (Rev3)
  hc-sr1 = hc-sr04
  J1 = Piezo Speaker
  LED1 = LED - 5mm [color="Red (633nm)" package="5 mm [THT]"]
  LED2 = LED - 5mm [color="Yellow (595nm)" package="5 mm [THT]"]
  R1 = Resistor [tolerance=±5% resistance=220 package=THT]
  R2 = Resistor [tolerance=±5% resistance=220 package=THT]

nets:
  N1: Componente1.D9_PWM, LED1.anode
  N2: Componente1.D10_PWM/SS, LED2.anode
  N3: Componente1.D11_PWM/MOSI, J1.pin2
  N4: Componente1.D12/MISO, hc-sr1.Echo
  N5: Componente1.D13/SCK, hc-sr1.Trig
  GND: Componente1.GND, hc-sr1.GND, R1.Pin_0, R2.Pin_0
  5V: Componente1.5V, hc-sr1.VCC
  N6: LED1.cathode, R2.Pin_1
  N7: LED2.cathode, R1.Pin_1
