# Fritzing sketch Fritzing (saved by Fritzing 0.8.7b)
breadboards: 1

parts:
  Parte1 = Arduino Uno (Rev3)
  R1 = Resistor [tolerance=±5% resistance=1k package=THT]
  Q1 = NPN-Transistor [package="TO92 [THT]"]
  R2 = Rotary Potentiometer (Small) [maximum_resistance=10kΩ package=THT]
  D1 = Rectifier Diode [part_number=1N4001 package="300 mil [THT]"]
  M1 = DC Motor

nets (from the schematic view):
  N1: Parte1.A0, R2.wiper
  N2: Parte1.D9_PWM, R1.Pin_0
  N3: Parte1.5V, R2.leg1, D1.cathode, M1.pin_1
  N4: Parte1.GND, Q1.E, R2.leg2
  N5: R1.Pin_1, Q1.B
  N6: Q1.C, D1.anode, M1.pin_2
