# Fritzing sketch Fritzing (saved by Fritzing 0.9.3b)
breadboards: 1

parts:
  J1 = Piezo Speaker
  LED1 = LED - 5mm [color="Red (633nm)" package="5 mm [THT]"]
  LED2 = LED - 5mm [color="Green (555nm)" package="5 mm [THT]"]
  R1 = Resistor [tolerance=±5% resistance=220 package=THT]
  R2 = Resistor [tolerance=±5% resistance=220 package=THT]
  Parte1 = Arduino Uno (Rev3)
  hc-sr1 = hc-sr04

nets:
  GND: J1.pin1, R1.Pin_0, R2.Pin_0, Parte1.GND, hc-sr1.GND
  N1: J1.pin2, Parte1.D9_PWM
  N2: LED1.cathode, R2.Pin_1
  N3: LED1.anode, Parte1.D10_PWM/SS
  N4: LED2.cathode, R1.Pin_1
  N5: LED2.anode, Parte1.D11_PWM/MOSI
  N6: Parte1.D12/MISO, hc-sr1.Echo
  N7: Parte1.D13/SCK, hc-sr1.Trig
  5V: Parte1.5V, hc-sr1.VCC
