# Fritzing sketch Fritzing (saved by Fritzing 0.9.3b)
circuit board: 8.46667cm x 5.64444cm
breadboards: 1

parts:
  IC2 = L293D [package=THT]
  S1 = Pushbutton [package="[THT]"]
  S2 = Pushbutton [package="[THT]"]
  S3 = Pushbutton [package="[THT]"]
  S4 = Pushbutton [package="[THT]"]
  S5 = Pushbutton [package="[THT]"]
  R1 = Resistor [tolerance=±5% resistance=10k package=THT]
  Arduino1 = Arduino Uno (Rev3)
  R2 = Resistor [tolerance=±5% resistance=10k package=THT]
  R3 = Resistor [tolerance=±5% resistance=10k package=THT]
  R4 = Resistor [tolerance=±5% resistance=10k package=THT]
  R5 = Resistor [tolerance=±5% resistance=10k package=THT]
  R6 = Resistor [tolerance=±5% resistance=10k package=THT]
  S8 = Pushbutton [package="[THT]"]
  BAT1 = BC9VPC [package=bc9vpc]
  M1 = DC Motor

nets:
  N1: IC2.Enable_1, IC2.+V, S1.Pin_3, S1.Pin_4, S2.Pin_3, S2.Pin_4, S3.Pin_3, S3.Pin_4, S4.Pin_3, S4.Pin_4, S5.Pin_3, S5.Pin_4, Arduino1.5V
  N2: IC2.In_1, Arduino1.D13/SCK
  N3: IC2.Out_1_(_Controlled_by_Enable_1_), M1.pin_2
  N4: IC2.0V, R1.Pin_1, Arduino1.GND, R2.Pin_1, R3.Pin_1, R4.Pin_1, R5.Pin_1, R6.Pin_1, BAT1.V-
  N5: IC2.Out_2_(_Controlled_by_Enable_1_), M1.pin_1
  N6: IC2.In_2, Arduino1.D12/MISO
  N7: IC2.+Vmotor, Arduino1.VIN, BAT1.V+
  N8: S1.Pin_1, S1.Pin_2, R1.Pin_0, Arduino1.D0/RX
  N9: S2.Pin_1, S2.Pin_2, Arduino1.D2, R2.Pin_0
  N10: S3.Pin_1, S3.Pin_2, Arduino1.D4, R3.Pin_0
  N11: S4.Pin_1, S4.Pin_2, Arduino1.D6_PWM, R4.Pin_0
  N12: S5.Pin_1, S5.Pin_2, Arduino1.D8, R5.Pin_0
  N13: Arduino1.D10_PWM/SS, R6.Pin_0, S8.Pin_2
