# Fritzing sketch Fritzing (saved by Fritzing 0.8.7b)
breadboards: 1

parts:
  J1 = Basic Servo
  Parte1 = Arduino Uno (Rev3)
  S1 = Pushbutton [package="[THT]"]
  R5 = Resistor [tolerance=±5% resistance=10k package=THT]
  LED1 = LED - 5mm [color="Red (633nm)" package="5 mm [THT]"]
  R1 = Resistor [tolerance=±5% resistance=220 package=THT]
  R3 = Resistor [tolerance=±5% resistance=220 package=THT]
  R2 = Resistor [tolerance=±5% resistance=220 package=THT]
  R4 = Resistor [tolerance=±5% resistance=220 package=THT]
  LED2 = LED - 5mm [color="Red (633nm)" package="5 mm [THT]"]
  LED3 = LED - 5mm [color="Green (570nm)" package="5 mm [THT]"]
  LED4 = LED - 5mm [color="Green (570nm)" package="5 mm [THT]"]
  U1 = TCMT1103-OPTO [package=ssop-4]
  R7 = Resistor [tolerance=±5% resistance=10k package=THT]
  R6 = Resistor [tolerance=±5% resistance=220 package=THT]

nets:
  GND: J1.gnd, Parte1.GND, R5.Pin_1, R1.Pin_1, R3.Pin_1, R2.Pin_1, R4.Pin_1, U1.K, R7.Pin_0
  VCC: J1.vcc, Parte1.5V, S1.Pin_3, S1.Pin_4, U1.C, R6.Pin_1
  N1: J1.pulse, Parte1.D9_PWM
  N2: Parte1.D10_PWM/SS, LED1.anode, LED4.anode
  N3: Parte1.D11_PWM/MOSI, LED2.anode, LED3.anode
  N4: Parte1.D2, S1.Pin_1, S1.Pin_2, R5.Pin_0
  N5: Parte1.D3_PWM, U1.E, R7.Pin_1
  N6: LED1.cathode, R1.Pin_0
  N7: R3.Pin_0, LED3.cathode
  N8: R2.Pin_0, LED2.cathode
  N9: R4.Pin_0, LED4.cathode
  N10: U1.A, R6.Pin_0
