# Fritzing sketch Fritzing (saved by Fritzing 0.9.0b)
breadboards: 1

parts:
  LED2 = LED - 5mm [color="Red (633nm)" package="5 mm [THT]"]
  Parte3 = SRF05 Ultrasonic Rangefinder
  J2 = Basic Servo
  LED7 = LED - 5mm [color="Green (555nm)" package="5 mm [THT]"]
  Parte5 = Arduino Uno (Rev3)
  LED8 = LED - 5mm [color="Red (633nm)" package="5 mm [THT]"]
  LED9 = LED - 5mm [color="Green (555nm)" package="5 mm [THT]"]
  R1 = Resistor [tolerance=±5% resistance=220 package=THT]
  R2 = Resistor [tolerance=±5% resistance=220 package=THT]
  R3 = Resistor [tolerance=±5% resistance=220 package=THT]
  R4 = Resistor [tolerance=±5% resistance=220 package=THT]
  J1 = Piezo Speaker
  Parte4 = SRF05 Ultrasonic Rangefinder
  J3 = Basic Servo

nets:
  N1: LED2.cathode, Parte5.D5_PWM
  N2: LED2.anode, R3.Pin_0
  VCC: Parte3.VCC, J2.vcc, Parte5.5V, Parte4.VCC, J3.vcc
  N3: Parte3.Trig, Parte5.D13/SCK
  N4: Parte3.Echo, Parte5.D12/MISO
  GND: Parte3.GND, J2.gnd, Parte5.GND, R1.Pin_1, R2.Pin_1, R3.Pin_1, R4.Pin_1, J1.pin1, Parte4.GND, J3.gnd
  N5: J2.pulse, Parte5.D9_PWM
  N6: LED7.cathode, Parte5.D4
  N7: LED7.anode, R4.Pin_0
  N8: Parte5.D8, J3.pulse
  N9: Parte5.D10_PWM/SS, Parte4.Echo
  N10: Parte5.D11_PWM/MOSI, Parte4.Trig
  N11: Parte5.D3_PWM, J1.pin2
  N12: Parte5.D6_PWM, LED9.cathode
  N13: Parte5.D7, LED8.cathode
  N14: LED8.anode, R1.Pin_0
  N15: LED9.anode, R2.Pin_0
