# Fritzing sketch Fritzing (saved by Fritzing 0.8.6b)
breadboards: 1

parts:
  LED1 = LED - 5mm [color="Yellow (595nm)" package="5 mm [THT]"]
  LED2 = LED - 5mm [color="Green (570nm)" package="5 mm [THT]"]
  LED3 = LED - 5mm [color="White (8000K)" package="5 mm [THT]"]
  LED4 = LED - 5mm [color="White (8000K)" package="5 mm [THT]"]
  LED5 = LED - 5mm [color="Green (570nm)" package="5 mm [THT]"]
  LED6 = LED - 5mm [color="Yellow (595nm)" package="5 mm [THT]"]
  LED7 = LED - 5mm [color="Red (633nm)" package="5 mm [THT]"]
  LED8 = LED - 5mm [color="Red (633nm)" package="5 mm [THT]"]
  R1 = Resistor [tolerance=±5% resistance=220 package=THT]
  R2 = Resistor [tolerance=±5% resistance=220 package=THT]
  R3 = Resistor [tolerance=±5% resistance=220 package=THT]
  R4 = Resistor [tolerance=±5% resistance=100 package=THT]
  R5 = Resistor [tolerance=±5% resistance=100 package=THT]
  R6 = Resistor [tolerance=±5% resistance=220 package=THT]
  R7 = Resistor [tolerance=±5% resistance=220 package=THT]
  R8 = Resistor [tolerance=±5% resistance=220 package=THT]
  Parte1 = Arduino Ethernet Shield (Rev3)

nets:
  N1: LED1.cathode, R2.Pin_0
  N2: LED1.anode, Parte1.SPI/D12
  N3: LED2.cathode, R3.Pin_0
  N4: LED2.anode, Parte1.PWM_D11
  N5: LED3.cathode, R4.Pin_0
  N6: LED3.anode, Parte1.ETH_CS
  N7: LED4.cathode, R5.Pin_0
  N8: LED4.anode, Parte1.PWM_D9
  N9: LED5.cathode, R6.Pin_0
  N10: LED5.anode, Parte1.D8
  N11: LED6.cathode, R7.Pin_0
  N12: LED6.anode, Parte1.D7
  N13: LED7.cathode, R1.Pin_0
  N14: LED7.anode, Parte1.SPI/D13
  N15: LED8.cathode, R8.Pin_0
  N16: LED8.anode, Parte1.PWM_D6
  N17: R1.Pin_1, R2.Pin_1, R3.Pin_1, R4.Pin_1, R5.Pin_1, R6.Pin_1, R7.Pin_1, R8.Pin_1, Parte1.GND
