# Fritzing sketch Fritzing (saved by Fritzing 0.9.3b)
breadboards: 1

parts:
  Componente1 = Arduino Uno (Rev3)
  LED1 = LED - 5mm [color="Red (633nm)" package="5 mm [THT]"]
  LED2 = LED - 5mm [color="Red (633nm)" package="5 mm [THT]"]
  LED3 = LED - 5mm [color="Red (633nm)" package="5 mm [THT]"]
  LED4 = LED - 5mm [color="Red (633nm)" package="5 mm [THT]"]
  LED5 = LED - 5mm [color="Red (633nm)" package="5 mm [THT]"]
  LED6 = LED - 5mm [color="Red (633nm)" package="5 mm [THT]"]
  LED7 = LED - 5mm [color="Red (633nm)" package="5 mm [THT]"]
  R1 = Resistor [tolerance=±5% resistance=220 package=THT]
  R2 = Resistor [tolerance=±5% resistance=220 package=THT]
  R3 = Resistor [tolerance=±5% resistance=220 package=THT]
  R4 = Resistor [tolerance=±5% resistance=220 package=THT]
  R5 = Resistor [tolerance=±5% resistance=220 package=THT]
  R6 = Resistor [tolerance=±5% resistance=220 package=THT]
  R8 = Resistor [tolerance=±5% resistance=220 package=THT]
  R9 = Rotary Potentiometer (Small) [maximum_resistance=10kΩ package=THT]

nets:
  N1: Componente1.A0, R9.wiper
  N2: Componente1.D10_PWM/SS, LED2.anode
  N3: Componente1.GND, R1.Pin_0, R2.Pin_0, R3.Pin_0, R4.Pin_0, R5.Pin_0, R6.Pin_0, R8.Pin_0, R9.leg2
  N4: Componente1.D2, LED1.anode
  N5: Componente1.D3_PWM, LED6.anode
  N6: Componente1.D4, LED5.anode
  N7: Componente1.D5_PWM, LED4.anode
  N8: Componente1.D6_PWM, LED7.anode
  N9: Componente1.D7, LED3.anode
  N10: Componente1.5V, R9.leg1
  N11: LED1.cathode, R8.Pin_1
  N12: LED2.cathode, R4.Pin_1
  N13: LED3.cathode, R5.Pin_1
  N14: LED4.cathode, R6.Pin_1
  N15: LED5.cathode, R3.Pin_1
  N16: LED6.cathode, R1.Pin_1
  N17: LED7.cathode, R2.Pin_1
