# Fritzing sketch Fritzing (saved by Fritzing 0.9.3b)
breadboards: 1

parts:
  Componente1 = Arduino Uno (Rev3)
  LED1 = LED - 5mm [color="Red (633nm)" package="5 mm [THT]"]
  LED2 = LED - 5mm [color="Red (633nm)" package="5 mm [THT]"]
  LED3 = LED - 5mm [color="Red (633nm)" package="5 mm [THT]"]
  LED4 = LED - 5mm [color="Yellow (595nm)" package="5 mm [THT]"]
  LED5 = LED - 5mm [color="Yellow (595nm)" package="5 mm [THT]"]
  LED6 = LED - 5mm [color="Yellow (595nm)" package="5 mm [THT]"]
  LED9 = LED - 5mm [color="Green (570nm)" package="5 mm [THT]"]
  LED8 = smd LED [color="Green (570nm)" package="0603 [SMD]"]
  LED7 = smd LED [color="Green (570nm)" package="0603 [SMD]"]
  R1 = Resistor [tolerance=±5% resistance=220 package=THT]
  R2 = Resistor [tolerance=±5% resistance=220 package=THT]
  R3 = Resistor [tolerance=±5% resistance=220 package=THT]
  R4 = Resistor [tolerance=±5% resistance=220 package=THT]
  R5 = Resistor [tolerance=±5% resistance=220 package=THT]
  R6 = Resistor [tolerance=±5% resistance=220 package=THT]
  R7 = Resistor [tolerance=±5% resistance=220 package=THT]
  R8 = Resistor [tolerance=±5% resistance=220 package=THT]
  R9 = Resistor [tolerance=±5% resistance=220 package=THT]

nets:
  N1: Componente1.D8, LED6.anode
  N2: Componente1.D9_PWM, LED5.anode
  N3: Componente1.D10_PWM/SS, LED4.anode
  N4: Componente1.D11_PWM/MOSI, LED3.anode
  N5: Componente1.D12/MISO, LED2.anode
  N6: Componente1.D13/SCK, LED1.anode
  N7: Componente1.GND, R1.Pin_1, R2.Pin_1, R3.Pin_1, R4.Pin_1, R5.Pin_1, R6.Pin_1, R7.Pin_1, R8.Pin_1, R9.Pin_1
  N8: Componente1.D5_PWM, LED9.anode
  N9: Componente1.D6_PWM, LED8.anode
  N10: Componente1.D7, LED7.anode
  N11: LED1.cathode, R1.Pin_0
  N12: LED2.cathode, R2.Pin_0
  N13: LED3.cathode, R3.Pin_0
  N14: LED4.cathode, R4.Pin_0
  N15: LED5.cathode, R5.Pin_0
  N16: LED6.cathode, R6.Pin_0
  N17: LED9.cathode, R9.Pin_0
  N18: LED8.cathode, R8.Pin_0
  N19: LED7.cathode, R7.Pin_0
