# Fritzing sketch Fritzing (saved by Fritzing 0.9.3b)
breadboards: 1

parts:
  R1 = Resistor [tolerance=±5% resistance=220 package=THT]
  LED1 = LED - 5mm [color="Green (570nm)" package="5 mm [THT]"]
  R2 = Resistor [tolerance=±5% resistance=220 package=THT]
  LED4 = LED - 5mm [color="Red (633nm)" package="5 mm [THT]"]
  LED5 = LED - 5mm [color="Red (633nm)" package="5 mm [THT]"]
  R4 = Resistor [tolerance=±5% resistance=220 package=THT]
  LED6 = LED - 5mm [color="Red (633nm)" package="5 mm [THT]"]
  R5 = Resistor [tolerance=±5% resistance=220 package=THT]
  R6 = Resistor [tolerance=±5% resistance=220 package=THT]
  R7 = Resistor [tolerance=±5% resistance=220 package=THT]
  LED7 = LED - 5mm [color="Green (570nm)" package="5 mm [THT]"]
  LED8 = LED - 5mm [color="Red (633nm)" package="5 mm [THT]"]
  LED9 = LED - 5mm [color="Red (633nm)" package="5 mm [THT]"]
  R8 = Resistor [tolerance=±5% resistance=220 package=THT]
  LED10 = LED - 5mm [color="Red (633nm)" package="5 mm [THT]"]
  R9 = Resistor [tolerance=±5% resistance=220 package=THT]
  R10 = Resistor [tolerance=±5% resistance=220 package=THT]
  R11 = Resistor [tolerance=±5% resistance=220 package=THT]
  LED11 = LED - 5mm [color="Green (570nm)" package="5 mm [THT]"]
  LED12 = LED - 5mm [color="Red (633nm)" package="5 mm [THT]"]
  LED13 = LED - 5mm [color="Red (633nm)" package="5 mm [THT]"]
  R12 = Resistor [tolerance=±5% resistance=220 package=THT]
  LED14 = LED - 5mm [color="Red (633nm)" package="5 mm [THT]"]
  R13 = Resistor [tolerance=±5% resistance=220 package=THT]
  S1 = Pushbutton [package="[THT]"]
  R14 = Resistor [tolerance=±5% resistance=10k package="2512 [SMD]"]
  J1 = Piezo Speaker
  Componente1 = Arduino Uno (Rev3)

nets:
  N1: R1.Pin_1, R2.Pin_1, R4.Pin_1, R5.Pin_1, R6.Pin_1, R7.Pin_1, R8.Pin_1, R9.Pin_1, R10.Pin_1, R11.Pin_1, R12.Pin_1, R13.Pin_1, R14.Pin_0, J1.pin1, Componente1.GND
  N2: LED1.anode, Componente1.D10_PWM/SS
  N3: LED4.anode, Componente1.A0
  N4: LED5.anode, Componente1.A1
  N5: LED6.anode, Componente1.D13/SCK
  N6: LED7.anode, Componente1.D6_PWM
  N7: LED8.anode, Componente1.D9_PWM
  N8: LED9.anode, Componente1.D8
  N9: LED10.anode, Componente1.D7
  N10: LED11.anode, Componente1.D2
  N11: LED12.anode, Componente1.D5_PWM
  N12: LED13.anode, Componente1.D4
  N13: LED14.anode, Componente1.D3_PWM
  N14: S1.Pin_1, S1.Pin_2, Componente1.5V
  N15: S1.Pin_3, S1.Pin_4, R14.Pin_1, Componente1.D11_PWM/MOSI
  N16: J1.pin2, Componente1.D12/MISO
