# Fritzing sketch Fritzing (saved by Fritzing 0.9.3b)
breadboards: 1

parts:
  Componente1 = Arduino Uno (Rev3)
  R1 = Resistor [tolerance=±5% resistance=220 package=THT]
  R2 = Resistor [tolerance=±5% resistance=220 package=THT]
  R3 = Resistor [tolerance=±5% resistance=220 package=THT]
  LED1 = LED - 5mm [color="Red (633nm)" package="5 mm [THT]"]
  LED2 = LED - 5mm [color="Yellow (595nm)" package="5 mm [THT]"]
  LED3 = LED - 5mm [color="Green (560nm)" package="5 mm [THT]"]
  LM35 = LM35 Temperature Sensor [package="TO92 [THT]"]
  K1 = Relay [part_number=FRS1B-S package=THT]
  K2 = Relay [part_number=FRS1B-S package=THT]
  J1 = Basic Servo
  S1 = Pushbutton [package="[THT]"]
  S2 = Pushbutton [package="[THT]"]
  S3 = Pushbutton [package="[THT]"]
  S4 = Pushbutton [package="[THT]"]
  R4 = Resistor [tolerance=±5% resistance=10k package=THT]
  R5 = Resistor [tolerance=±5% resistance=10k package=THT]
  R6 = Resistor [tolerance=±5% resistance=10k package=THT]
  R7 = Resistor [tolerance=±5% resistance=10k package=THT]
  LCD_con_I2C = LCD screen

nets:
  N1: Componente1.A0, LM35.Vout
  N2: Componente1.A4/SDA, LCD_con_I2C.DB0
  N3: Componente1.A5/SCL, LCD_con_I2C.E
  N4: Componente1.D8, LED3.cathode
  N5: Componente1.D9_PWM, LED2.cathode
  N6: Componente1.D10_PWM/SS, LED1.cathode
  5V: Componente1.D11_PWM/MOSI, Componente1.D12/MISO, Componente1.D13/SCK, Componente1.D3_PWM, Componente1.D6_PWM, Componente1.5V, LM35.+Vs, K1.COIL1, K1.C1, K1.C2, K2.C1, K2.C2, J1.vcc, S1.Pin_3, S1.Pin_4, S2.Pin_3, S2.Pin_4, S3.Pin_3, S3.Pin_4, S4.Pin_3, S4.Pin_4, R4.Pin_0, R5.Pin_0, R6.Pin_0, R7.Pin_0, LCD_con_I2C.VDD
  GND: Componente1.GND, R1.Pin_1, R2.Pin_1, R3.Pin_1, LM35.GND, J1.gnd, R4.Pin_1, R5.Pin_1, R6.Pin_1, R7.Pin_1, LCD_con_I2C.VSS
  N7: Componente1.D5_PWM, J1.pulse
  N8: Componente1.D7, K1.COIL2
  N9: R1.Pin_0, LED1.anode
  N10: R2.Pin_0, LED2.anode
  N11: R3.Pin_0, LED3.anode
  N12: S1.Pin_1, S1.Pin_2
  N13: S2.Pin_1, S2.Pin_2
  N14: S3.Pin_1, S3.Pin_2
  N15: S4.Pin_1, S4.Pin_2
  N16: LCD_con_I2C.DB2, LCD_con_I2C.DB3
