# Fritzing sketch Fritzing (saved by Fritzing 0.8.6b)
breadboards: 1

parts:
  R1 = Resistor [tolerance=±5% resistance=220 package=THT]
  LED1 = LED - 5mm [color="Red (633nm)" package="5 mm [THT]"]
  Parte1 = Arduino Uno (Rev3)
  SPKR1 = Loudspeaker
  R2 = Resistor [tolerance=±5% resistance=100 package=THT]

nets:
  N1: R1.Pin_0, Parte1.GND, R2.Pin_0
  N2: R1.Pin_1, LED1.cathode
  N3: LED1.anode, Parte1.D2
  N4: Parte1.D4, SPKR1.pin2
  N5: SPKR1.pin1, R2.Pin_1
