# Fritzing sketch Esquema-eléctrico (saved by Fritzing 0.9.3b)

parts:
  Arduino1 = Arduino Uno (Rev3)
  J1 = Basic Servo

nets:
  N1: Arduino1.D9_PWM, J1.pulse
  GND: Arduino1.GND, J1.gnd
  5V: Arduino1.5V, J1.vcc
