# Fritzing sketch Esquema-eléctrico (saved by Fritzing 0.9.3b)
breadboards: 1

parts:
  Arduino1 = Arduino Uno (Rev3)
  R1 = Resistor [tolerance=±5% resistance=220 package=THT]
  R2 = Resistor [tolerance=±5% resistance=220 package=THT]
  LED1 = LED - 5mm [color="Red (633nm)" package="5 mm [THT]"]
  LED2 = LED - 5mm [color="Green (555nm)" package="5 mm [THT]"]

nets:
  N1: Arduino1.D12/MISO, LED2.anode
  N2: Arduino1.D13/SCK, LED1.anode
  N3: Arduino1.GND, R1.Pin_1, R2.Pin_1
  N4: R1.Pin_0, LED2.cathode
  N5: R2.Pin_0, LED1.cathode
