# Fritzing sketch Esquema-eléctrico (saved by Fritzing 0.9.3b)
breadboards: 1

parts:
  Arduino1 = Arduino Uno (Rev3)
  LED2 = RGB LED - (4 legs) [package="5 mm [THT]"]
  R1 = Resistor [tolerance=±5% resistance=220 package=THT]
  R2 = Resistor [tolerance=±5% resistance=100 package=THT]
  R3 = Resistor [tolerance=±5% resistance=100 package=THT]

nets:
  N1: Arduino1.D9_PWM, R1.Pin_0
  N2: Arduino1.D5_PWM, R3.Pin_1
  N3: Arduino1.D6_PWM, R2.Pin_1
  N4: Arduino1.5V, LED2.common_anode
  N5: LED2.red_cathode, R1.Pin_1
  N6: LED2.green_cathode, R2.Pin_0
  N7: LED2.blue_cathode, R3.Pin_0
